// Logisim project cpu.circ as structural Verilog: 1 circuit, main circuit main
module main (
  input  [31:0] INSTRUCTION,
  input  CLOCK,
  output [31:0] FETCH_ADDRESS,
  output [31:0] s0_Value,
  output [31:0] s1_Value,
  output [31:0] s2_Value,
  output [31:0] ra_Value,
  output [31:0] sp_Value
);

  wire ALUSrc, eql, ExtOp, main_2_signed_overflow, main_3_p1, main_3_p2, main_3_p7, main_3_p11, main_3_p13,
       MemToReg, MemWr, RegDst, RegWr;
  wire [1:0] nPCsel;
  wire [3:0] ALUCtr;
  wire [4:0] multiplexer_1_out;
  wire [31:0] adder_2_out, immed, main_1_read_data_1, main_2_result, main_3_p9, multiplexer_2_out,
       multiplexer_3_out, multiplexer_4_out, PC_4, rt, shifter_1_out, shifter_2_out, WrtData;

  Adder #(.width(32)) adder_1 (.a(INSTRUCTION), .b(32'h4), .out(PC_4));  // open: cin, cout
  Multiplexer #(.width(5), .enable("false")) multiplexer_1 (
    .in0(INSTRUCTION[20:16]), .in1(INSTRUCTION[15:11]), .out(multiplexer_1_out), .sel(RegDst));
  assign immed = {{16{ExtOp}}, INSTRUCTION[15:0]};  // Bit_Extender bit_extender_1
  Shifter #(.width(32)) shifter_1 (.in(immed), .\dist (5'b00010), .out(shifter_1_out));
  Shifter #(.width(32)) shifter_2 (.in(INSTRUCTION), .\dist (5'b00010), .out(shifter_2_out));
  regfile_main main_1 (
    .Read_Register_1(INSTRUCTION[25:21]), .Read_Register_2(INSTRUCTION[20:16]),
    .Write_Register(multiplexer_1_out), .Write_Data(WrtData), .Write_Enable(RegWr), .Clock(CLOCK),
    .Read_Data_1(main_1_read_data_1), .Read_Data_2(rt), .s0_Value(s0_Value), .s1_Value(s1_Value),
    .s2_Value(s2_Value), .ra_Value(ra_Value), .sp_Value(sp_Value));
  Adder #(.width(32)) adder_2 (.a(PC_4), .b(shifter_1_out), .out(adder_2_out));  // open: cin, cout
  Multiplexer #(.width(32), .enable("false")) multiplexer_2 (
    .in0(rt), .in1(immed), .out(multiplexer_2_out), .sel(ALUSrc));
  Multiplexer #(.width(32), .enable("false")) multiplexer_3 (
    .in0(PC_4), .in1(adder_2_out), .out(multiplexer_3_out), .sel(eql));
  LED led_1 (.in(main_2_signed_overflow));
  alu_main main_2 (
    .Switch(ALUCtr), .X(main_1_read_data_1), .Equal(eql), .Result(main_2_result),
    .Signed_Overflow(main_2_signed_overflow), .Y(multiplexer_2_out));
  Multiplexer #(.select(2), .width(32), .enable("false")) multiplexer_4 (
    .in0(PC_4), .in1(multiplexer_3_out), .in2({PC_4[31:28], shifter_2_out[27:0]}), .out(multiplexer_4_out),
    .sel(nPCsel));  // open: in3
  Register #(.width(32)) PC (.D(multiplexer_4_out), .Q(FETCH_ADDRESS), .clk(CLOCK));  // open: en, clr
  // mem_main main_3: pin names not known; wires that end beside it: main_3_p1, main_3_p2, main_3_p2, main_2_result, rt, MemWr, main_3_p7, CLOCK, main_3_p9, main_3_p7, main_3_p11, main_3_p11, main_3_p13, main_3_p13, main_3_p1
  Multiplexer #(.width(32), .enable("false")) multiplexer_5 (
    .in0(main_2_result), .in1(main_3_p9), .out(WrtData), .sel(MemToReg));

  // Other names for the same wires on the sheet: clk = CLOCK; fetch_addr[31:0] = FETCH_ADDRESS;
  //   funct[5:0] = INSTRUCTION[5:0]; opcode[5:0] = INSTRUCTION[31:26]; ra[31:0] = ra_Value; s0[31:0] = s0_Value;
  //   s1[31:0] = s1_Value; s2[31:0] = s2_Value; sp[31:0] = sp_Value

  // Notes on the sheet:
  //   Output
  //   These are outputs/inputs from run.circ
  //   Inputs
  //   These are DEBUG/TEST outputs from your circuit.
endmodule
